// Logisim project part1.circ as structural Verilog: 4 circuits, main circuit main
module main (
);


  // Notes on the sheet:
  //   cs31 lab3, part 1
  //   Yael Borger, Arina Kazakova
endmodule

module signext2to4 (
  input  in_1,
  input  in_2,
  output out_3,
  output out_4,
  output out_5,
  output out_6
);


  assign out_3 = in_1;
  assign out_4 = in_2;
  assign out_5 = in_2;
  assign out_6 = in_2;
endmodule

module fulladder (
  input  X,
  input  Y,
  input  Carry_In,
  output Sum,
  output Carry_Out
);

  wire and_1_out, and_2_out, xor_1_out;

  xor xor_1 (xor_1_out, X, Y);
  and and_1 (and_1_out, X, Y);
  xor xor_2 (Sum, xor_1_out, Carry_In);
  and and_2 (and_2_out, xor_1_out, Carry_In);
  or or_1 (Carry_Out, and_2_out, and_1_out);
endmodule

module fulladder4 (
  input  [3:0] X,
  input  [3:0] Y,
  input  Carry__In,
  output [3:0] Answer,
  output Carry_Out
);

  wire fulladder_1_carry_out, fulladder_3_carry_out;

  fulladder fulladder_1 (.X(X[3]), .Y(Y[3]), .Carry_In(Carry__In), .Sum(Answer[3]), .Carry_Out(fulladder_1_carry_out));
  fulladder fulladder_2 (.X(X[2]), .Y(Y[2]), .Carry_In(fulladder_1_carry_out), .Sum(Answer[2]), .Carry_Out(Answer[2]));
  fulladder fulladder_3 (.X(X[1]), .Y(Y[1]), .Carry_In(Answer[2]), .Sum(Answer[1]), .Carry_Out(fulladder_3_carry_out));
  fulladder fulladder_4 (.X(X[0]), .Y(Y[0]), .Carry_In(fulladder_3_carry_out), .Sum(Answer[0]), .Carry_Out(Carry_Out));
endmodule
